// Digital circuit MyFirstProcessor.dig as structural Verilog
module MyFirstProcessor (
  input  in_1,
  input  clk
);

  wire _74161_1_pin1, _74161_1_pin2, _74161_1_pin3, _74161_1_pin4, _74161_1_pin5, _74161_1_pin6,
       _74161_2_pin1, _74161_2_pin11, _74161_2_pin12, _74161_2_pin13, _74161_2_pin14, _74173_4_pin3,
       _74173_4_pin4, _74173_4_pin5, _74173_4_pin6, _74238_1_pin10, _74238_1_pin11, _74238_1_pin12,
       _74238_1_pin13, _74238_1_pin14, _74238_1_pin15, _74283_1_pin7, _74283_1_pin9, _74541_1_pin2,
       _74541_1_pin3, _74541_1_pin4, _74541_1_pin5, _74541_4_pin2, _74541_4_pin3, _74541_4_pin4,
       _74541_4_pin5, A1, A2, A3, A4, A5, A6, A7, A8, AI, AO, B1, B2, B3, B4, B5, B6, B7, B8, BI, BO, BUS0,
       BUS1, BUS2, BUS3, BUS4, BUS5, BUS6, BUS7, CF, CFI, CLK_t, DMAI, DMI, DMO, H_sA, H_sB, H_sC, H_sD,
       H_sE, H_sF, H_sG, HLT, IMAI, IMI, IMO, IRI, IRO, J, multiplexer_1_out, multiplexer_2_out, nor_1_out,
       not_18_out, NXT, O_sA, O_sB, O_sC, O_sD, O_sE, O_sF, O_sG, or_1_out, OUT, PCE, PCO, RES, S1, S2, S3,
       S4, S5, S6, S7, S8, SgnA, SgnB, SgnC, SgnD, SgnE, SgnF, SgnG, SUB, SUMO, T_sA, T_sB, T_sC, T_sD, T_sE,
       T_sF, T_sG, Y1, Y2, Y3, Y4, Y5, Y6, Y7, Y8, ZF, ZFI;
  wire [3:0] _74173_2_pin4, _74173_3_pin4;
  wire [7:0] _74173_1_pin6, _74377_1_pin19, eepromdualport_1_d, ramdualport_1_d;
  wire [7:7] eeprom_2_d, eeprom_3_d, eeprom_4_d, eeprom_5_d;
  wire [19:0] eeprom_1_d;

  _74161 _74161_1 (
    .pin1(_74161_1_pin1), .pin2(_74161_1_pin2), .pin3(_74161_1_pin3), .pin4(_74161_1_pin4),
    .pin5(_74161_1_pin5), .pin6(_74161_1_pin6), .pin7(1'b1), .pin8(1'b0), .pin9(1'b1), .pin10(1'b1),
    .pin12(_74173_1_pin6[2]), .pin13(_74173_1_pin6[1]), .pin14(_74173_1_pin6[0]), .pin16(1'b1));  // open: pin11, pin15
  not not_1 (_74161_1_pin1, or_1_out);
  or or_1 (or_1_out, RES, NXT, _74238_1_pin10);
  // NotConnected on _74161_1_pin3
  not not_2 (_74161_1_pin2, CLK_t);
  // NotConnected on _74161_1_pin5
  // NotConnected on _74161_1_pin4
  // NotConnected on _74161_1_pin6
  LED led_1 (.in(_74238_1_pin15));
  _74238 _74238_1 (
    .pin1(_74173_1_pin6[0]), .pin2(_74173_1_pin6[1]), .pin3(_74173_1_pin6[2]), .pin4(1'b0), .pin5(1'b0),
    .pin6(1'b1), .pin8(1'b0), .pin10(_74238_1_pin10), .pin11(_74238_1_pin11), .pin12(_74238_1_pin12),
    .pin13(_74238_1_pin13), .pin14(_74238_1_pin14), .pin15(_74238_1_pin15), .pin16(1'b1));  // open: pin7, pin9
  _74173 _74173_1 (
    .pin1(1'b0), .pin2(1'b0), .pin3(_74173_1_pin6[7]), .pin4(_74173_1_pin6[6]), .pin5(_74173_1_pin6[5]),
    .pin6(_74173_1_pin6[4]), .pin7(CLK_t), .pin8(1'b0), .pin9(IRI), .pin10(IRI), .pin11(BUS4), .pin12(BUS5),
    .pin13(BUS6), .pin14(BUS7), .pin15(RES), .pin16(1'b1));
  LED led_2 (.in(_74238_1_pin13));
  LED led_3 (.in(_74238_1_pin14));
  _74173 _74173_2 (
    .pin1(1'b0), .pin2(1'b0), .pin3(_74173_2_pin4[3]), .pin4(_74173_2_pin4[2]), .pin5(_74173_2_pin4[1]),
    .pin6(_74173_2_pin4[0]), .pin7(CLK_t), .pin8(1'b0), .pin9(DMAI), .pin10(DMAI), .pin11(BUS0),
    .pin12(BUS1), .pin13(BUS2), .pin14(BUS3), .pin15(RES), .pin16(1'b1));
  LED led_4 (.in(_74238_1_pin12));
  LED led_5 (.in(_74238_1_pin11));
  _74173 _74173_3 (
    .pin1(1'b0), .pin2(1'b0), .pin3(_74173_3_pin4[3]), .pin4(_74173_3_pin4[2]), .pin5(_74173_3_pin4[1]),
    .pin6(_74173_3_pin4[0]), .pin7(CLK_t), .pin8(1'b0), .pin9(IMAI), .pin10(IMAI), .pin11(BUS0),
    .pin12(BUS1), .pin13(BUS2), .pin14(BUS3), .pin15(RES), .pin16(1'b1));
  LED led_6 (.in(_74173_2_pin4[3]));
  LED led_7 (.in(_74173_2_pin4[2]));
  LED led_8 (.in(_74173_3_pin4[3]));
  LED led_9 (.in(_74173_3_pin4[2]));
  LED led_10 (.in(_74173_2_pin4[1]));
  LED led_11 (.in(_74173_2_pin4[0]));
  _74161 _74161_2 (
    .pin1(_74161_2_pin1), .pin2(CLK_t), .pin3(BUS0), .pin4(BUS1), .pin5(BUS2), .pin6(BUS3), .pin7(PCE),
    .pin8(1'b0), .pin9(J), .pin10(PCE), .pin11(_74161_2_pin11), .pin12(_74161_2_pin12),
    .pin13(_74161_2_pin13), .pin14(_74161_2_pin14), .pin16(1'b1));  // open: pin15
  not not_3 (_74161_2_pin1, RES);
  LED led_12 (.in(_74173_3_pin4[1]));
  LED led_13 (.in(_74173_3_pin4[0]));
  _74173 _74173_4 (
    .pin1(1'b0), .pin2(1'b0), .pin3(_74173_4_pin3), .pin4(_74173_4_pin4), .pin5(_74173_4_pin5),
    .pin6(_74173_4_pin6), .pin7(CLK_t), .pin8(1'b0), .pin9(IRI), .pin10(IRI), .pin11(BUS0), .pin12(BUS1),
    .pin13(BUS2), .pin14(BUS3), .pin15(RES), .pin16(1'b1));
  LED led_14 (.in(CFI));
  LED led_15 (.in(ZFI));
  LED led_16 (.in(DMI));
  LED led_17 (.in(eeprom_1_d[19]));
  not not_4 (DMAI, eeprom_1_d[19]);
  LED led_18 (.in(NXT));
  LED led_19 (.in(eeprom_1_d[17]));
  not not_5 (DMO, eeprom_1_d[17]);
  LED led_20 (.in(eeprom_1_d[14]));
  LED led_21 (.in(HLT));
  not not_6 (IMAI, eeprom_1_d[14]);
  EEPROMDualPort #(.AddrBits(4), .isProgramMemory("true"), .Bits(8)) eepromdualport_1 (
    .A(_74173_3_pin4), .Din({8{1'b0}}), .str(IMI), .C(CLK_t), .ld(1'b1), .D(eepromdualport_1_d));
  RAMDualPort #(.AddrBits(4), .Bits(8)) ramdualport_1 (
    .A(_74173_2_pin4), .Din({BUS7, BUS6, BUS5, BUS4, BUS3, BUS2, BUS1, BUS0}), .str(DMI), .C(CLK_t),
    .ld(1'b1), .D(ramdualport_1_d));
  LED led_22 (.in(eeprom_1_d[12]));
  LED led_23 (.in(IMI));
  not not_7 (IMO, eeprom_1_d[12]);
  LED led_24 (.in(eeprom_1_d[10]));
  LED led_25 (.in(eeprom_1_d[11]));
  not not_8 (IRI, eeprom_1_d[10]);
  not not_9 (IRO, eeprom_1_d[11]);
  _74541 _74541_1 (
    .pin1(PCO), .pin2(_74541_1_pin2), .pin3(_74541_1_pin3), .pin4(_74541_1_pin4), .pin5(_74541_1_pin5),
    .pin6(_74161_2_pin11), .pin7(_74161_2_pin12), .pin8(_74161_2_pin13), .pin9(_74161_2_pin14), .pin10(1'b0),
    .pin11(BUS0), .pin12(BUS1), .pin13(BUS2), .pin14(BUS3), .pin19(PCO), .pin20(1'b1));  // open: pin15, pin16, pin17, pin18
  // NotConnected on _74541_1_pin2
  _74541 _74541_2 (
    .pin1(IMO), .pin2(eepromdualport_1_d[7]), .pin3(eepromdualport_1_d[6]), .pin4(eepromdualport_1_d[5]),
    .pin5(eepromdualport_1_d[4]), .pin6(eepromdualport_1_d[3]), .pin7(eepromdualport_1_d[2]),
    .pin8(eepromdualport_1_d[1]), .pin9(eepromdualport_1_d[0]), .pin10(1'b0), .pin11(BUS0), .pin12(BUS1),
    .pin13(BUS2), .pin14(BUS3), .pin15(BUS4), .pin16(BUS5), .pin17(BUS6), .pin18(BUS7), .pin19(IMO),
    .pin20(1'b1));
  LED led_26 (.in(eepromdualport_1_d[7]));
  _74541 _74541_3 (
    .pin1(DMO), .pin2(ramdualport_1_d[7]), .pin3(ramdualport_1_d[6]), .pin4(ramdualport_1_d[5]),
    .pin5(ramdualport_1_d[4]), .pin6(ramdualport_1_d[3]), .pin7(ramdualport_1_d[2]),
    .pin8(ramdualport_1_d[1]), .pin9(ramdualport_1_d[0]), .pin10(1'b0), .pin11(BUS0), .pin12(BUS1),
    .pin13(BUS2), .pin14(BUS3), .pin15(BUS4), .pin16(BUS5), .pin17(BUS6), .pin18(BUS7), .pin19(DMO),
    .pin20(1'b1));
  LED led_27 (.in(ramdualport_1_d[7]));
  _74541 _74541_4 (
    .pin1(IRO), .pin2(_74541_4_pin2), .pin3(_74541_4_pin3), .pin4(_74541_4_pin4), .pin5(_74541_4_pin5),
    .pin6(_74173_4_pin3), .pin7(_74173_4_pin4), .pin8(_74173_4_pin5), .pin9(_74173_4_pin6), .pin10(1'b0),
    .pin11(BUS0), .pin12(BUS1), .pin13(BUS2), .pin14(BUS3), .pin19(IRO), .pin20(1'b1));  // open: pin15, pin16, pin17, pin18
  // NotConnected on _74541_4_pin2
  LED led_28 (.in(_74173_1_pin6[7]));
  EEPROM #(.AddrBits(10), .isProgramMemory("true"), .Bits(22)) eeprom_1 (
    .A({CF, ZF, _74173_1_pin6[7:4], 1'b0, _74173_1_pin6[2:0]}), .CS(1'b1), .WE(1'b0), .OE(1'b1),
    .D({ZFI, CFI, eeprom_1_d[19], DMI, eeprom_1_d[17], NXT, HLT, eeprom_1_d[14], IMI, eeprom_1_d[12:7], SUB, eeprom_1_d[5:3], PCE, eeprom_1_d[1:0]}));
  LED led_29 (.in(eeprom_1_d[8]));
  LED led_30 (.in(eeprom_1_d[9]));
  not not_10 (AO, eeprom_1_d[8]);
  not not_11 (AI, eeprom_1_d[9]);
  // NotConnected on _74541_1_pin4
  // NotConnected on _74541_1_pin3
  LED led_31 (.in(eepromdualport_1_d[6]));
  LED led_32 (.in(eepromdualport_1_d[5]));
  LED led_33 (.in(ramdualport_1_d[6]));
  LED led_34 (.in(ramdualport_1_d[5]));
  // NotConnected on _74541_4_pin4
  // NotConnected on _74541_4_pin3
  LED led_35 (.in(_74173_1_pin6[6]));
  LED led_36 (.in(_74173_1_pin6[5]));
  LED led_37 (.in(SUB));
  LED led_38 (.in(eeprom_1_d[7]));
  not not_12 (SUMO, eeprom_1_d[7]);
  // NotConnected on _74541_1_pin5
  LED led_39 (.in(_74161_2_pin11));
  LED led_40 (.in(eepromdualport_1_d[3]));
  LED led_41 (.in(eepromdualport_1_d[4]));
  LED led_42 (.in(ramdualport_1_d[3]));
  LED led_43 (.in(ramdualport_1_d[4]));
  // NotConnected on _74541_4_pin5
  LED led_44 (.in(_74173_4_pin3));
  LED led_45 (.in(_74173_1_pin6[4]));
  LED led_46 (.in(eeprom_1_d[4]));
  LED led_47 (.in(eeprom_1_d[5]));
  not not_13 (BI, eeprom_1_d[4]);
  not not_14 (BO, eeprom_1_d[5]);
  LED led_48 (.in(_74161_2_pin13));
  LED led_49 (.in(_74161_2_pin12));
  LED led_50 (.in(eepromdualport_1_d[2]));
  LED led_51 (.in(eepromdualport_1_d[1]));
  LED led_52 (.in(ramdualport_1_d[2]));
  LED led_53 (.in(ramdualport_1_d[1]));
  LED led_54 (.in(_74173_4_pin4));
  LED led_55 (.in(_74173_4_pin5));
  LED led_56 (.in(PCE));
  LED led_57 (.in(eeprom_1_d[3]));
  not not_15 (OUT, eeprom_1_d[3]);
  LED led_58 (.in(_74161_2_pin14));
  LED led_59 (.in(eepromdualport_1_d[0]));
  LED led_60 (.in(ramdualport_1_d[0]));
  LED led_61 (.in(_74173_4_pin6));
  LED led_62 (.in(eeprom_1_d[0]));
  LED led_63 (.in(eeprom_1_d[1]));
  not not_16 (PCO, eeprom_1_d[1]);
  not not_17 (J, eeprom_1_d[0]);
  PullDown pulldown_1 (.out(BUS7));
  PullDown pulldown_2 (.out(BUS3));
  PullDown pulldown_3 (.out(BUS4));
  PullDown pulldown_4 (.out(BUS5));
  PullDown pulldown_5 (.out(BUS6));
  PullDown pulldown_6 (.out(BUS0));
  PullDown pulldown_7 (.out(BUS1));
  PullDown pulldown_8 (.out(BUS2));
  _74541 _74541_5 (
    .pin1(AO), .pin2(A8), .pin3(A7), .pin4(A6), .pin5(A5), .pin6(A4), .pin7(A3), .pin8(A2), .pin9(A1),
    .pin10(1'b0), .pin11(BUS0), .pin12(BUS1), .pin13(BUS2), .pin14(BUS3), .pin15(BUS4), .pin16(BUS5),
    .pin17(BUS6), .pin18(BUS7), .pin19(AO), .pin20(1'b1));
  _74541 _74541_6 (
    .pin1(SUMO), .pin2(S8), .pin3(S7), .pin4(S6), .pin5(S5), .pin6(S4), .pin7(S3), .pin8(S2), .pin9(S1),
    .pin10(1'b0), .pin11(BUS0), .pin12(BUS1), .pin13(BUS2), .pin14(BUS3), .pin15(BUS4), .pin16(BUS5),
    .pin17(BUS6), .pin18(BUS7), .pin19(SUMO), .pin20(1'b1));
  _74541 _74541_7 (
    .pin1(BO), .pin2(B8), .pin3(B7), .pin4(B6), .pin5(B5), .pin6(B4), .pin7(B3), .pin8(B2), .pin9(B1),
    .pin10(1'b0), .pin11(BUS0), .pin12(BUS1), .pin13(BUS2), .pin14(BUS3), .pin15(BUS4), .pin16(BUS5),
    .pin17(BUS6), .pin18(BUS7), .pin19(BO), .pin20(1'b1));
  LED led_64 (.in(A8));
  LED led_65 (.in(A7));
  LED led_66 (.in(S8));
  LED led_67 (.in(S7));
  LED led_68 (.in(B8));
  LED led_69 (.in(B7));
  Seven_Seg #(.persistTime(14)) seven_seg_1 (
    .a(SgnA), .b(SgnB), .c(SgnC), .d(SgnD), .e(SgnE), .f(SgnF), .g(SgnG), .dp(1'b0));
  LED led_70 (.in(A6));
  LED led_71 (.in(A5));
  LED led_72 (.in(S6));
  LED led_73 (.in(S5));
  LED led_74 (.in(B6));
  LED led_75 (.in(B5));
  Seven_Seg seven_seg_2 (.a(H_sA), .b(H_sB), .c(H_sC), .d(H_sD), .e(H_sE), .f(H_sF), .g(H_sG), .dp(1'b0));
  not not_18 (not_18_out, HLT);
  LED led_76 (.in(A4));
  LED led_77 (.in(A3));
  LED led_78 (.in(S4));
  LED led_79 (.in(S3));
  LED led_80 (.in(B4));
  LED led_81 (.in(B3));
  Seven_Seg seven_seg_3 (.a(T_sA), .b(T_sB), .c(T_sC), .d(T_sD), .e(T_sE), .f(T_sF), .g(T_sG), .dp(1'b0));
  and and_1 (CLK_t, clk, not_18_out);
  LED led_82 (.in(A2));
  LED led_83 (.in(A1));
  LED led_84 (.in(S2));
  LED led_85 (.in(S1));
  LED led_86 (.in(B2));
  LED led_87 (.in(B1));
  Seven_Seg seven_seg_4 (.a(O_sA), .b(O_sB), .c(O_sC), .d(O_sD), .e(O_sE), .f(O_sF), .g(O_sG), .dp(1'b0));
  _74173 _74173_5 (
    .pin1(1'b0), .pin2(1'b0), .pin3(A8), .pin4(A7), .pin5(A6), .pin6(A5), .pin7(CLK_t), .pin8(1'b0),
    .pin9(AI), .pin10(AI), .pin11(BUS4), .pin12(BUS5), .pin13(BUS6), .pin14(BUS7), .pin15(RES), .pin16(1'b1));
  _74283 _74283_1 (
    .pin1(S6), .pin2(Y6), .pin3(A6), .pin4(S5), .pin5(A5), .pin6(Y5), .pin7(_74283_1_pin7), .pin8(1'b0),
    .pin9(_74283_1_pin9), .pin10(S8), .pin11(Y8), .pin12(A8), .pin13(S7), .pin14(A7), .pin15(Y7), .pin16(1'b1));
  _74173 _74173_6 (
    .pin1(1'b0), .pin2(1'b0), .pin3(B8), .pin4(B7), .pin5(B6), .pin6(B5), .pin7(CLK_t), .pin8(1'b0),
    .pin9(BI), .pin10(BI), .pin11(BUS4), .pin12(BUS5), .pin13(BUS6), .pin14(BUS7), .pin15(RES), .pin16(1'b1));
  _74377 _74377_1 (
    .pin1(OUT), .pin2(_74377_1_pin19[0]), .pin3(BUS0), .pin4(BUS1), .pin5(_74377_1_pin19[1]),
    .pin6(_74377_1_pin19[2]), .pin7(BUS2), .pin8(BUS3), .pin9(_74377_1_pin19[3]), .pin10(1'b0),
    .pin11(CLK_t), .pin12(_74377_1_pin19[4]), .pin13(BUS4), .pin14(BUS5), .pin15(_74377_1_pin19[5]),
    .pin16(_74377_1_pin19[6]), .pin17(BUS6), .pin18(BUS7), .pin19(_74377_1_pin19[7]), .pin20(1'b1));
  Button button_1 (.out(RES));
  nor nor_1 (nor_1_out, S8, S7, S6, S5, S4, S3, S2, S1);
  _74173 _74173_7 (
    .pin1(1'b0), .pin2(1'b0), .pin3(A4), .pin4(A3), .pin5(A2), .pin6(A1), .pin7(CLK_t), .pin8(1'b0),
    .pin9(AI), .pin10(AI), .pin11(BUS0), .pin12(BUS1), .pin13(BUS2), .pin14(BUS3), .pin15(RES), .pin16(1'b1));
  Multiplexer multiplexer_1 (.sel(ZFI), .in_0(ZF), .in_1(nor_1_out), .out(multiplexer_1_out));
  Multiplexer multiplexer_2 (.sel(CFI), .in_0(CF), .in_1(_74283_1_pin9), .out(multiplexer_2_out));
  _74283 _74283_2 (
    .pin1(S2), .pin2(Y2), .pin3(A2), .pin4(S1), .pin5(A1), .pin6(Y1), .pin7(SUB), .pin8(1'b0),
    .pin9(_74283_1_pin7), .pin10(S4), .pin11(Y4), .pin12(A4), .pin13(S3), .pin14(A3), .pin15(Y3), .pin16(1'b1));
  _74173 _74173_8 (
    .pin1(1'b0), .pin2(1'b0), .pin3(B4), .pin4(B3), .pin5(B2), .pin6(B1), .pin7(CLK_t), .pin8(1'b0),
    .pin9(BI), .pin10(BI), .pin11(BUS0), .pin12(BUS1), .pin13(BUS2), .pin14(BUS3), .pin15(RES), .pin16(1'b1));
  D_FF d_ff_1 (.D(multiplexer_1_out), .C(CLK_t), .Q(ZF));  // open: nQ
  D_FF d_ff_2 (.D(multiplexer_2_out), .C(CLK_t), .Q(CF));  // open: nQ
  LED led_88 (.in(ZF));
  LED led_89 (.in(CF));
  _7486 _7486_1 (
    .pin1(SUB), .pin2(B5), .pin3(Y5), .pin4(SUB), .pin5(B6), .pin6(Y6), .pin7(1'b0), .pin8(Y7), .pin9(SUB),
    .pin10(B7), .pin11(Y8), .pin12(SUB), .pin13(B8), .pin14(1'b1));
  EEPROM #(.AddrBits(9), .isProgramMemory("true"), .Bits(8)) eeprom_2 (
    .A({in_1, _74377_1_pin19}), .CS(1'b1), .WE(1'b0), .OE(1'b1),
    .D({eeprom_2_d[7], SgnA, SgnB, SgnC, SgnD, SgnE, SgnF, SgnG}));
  EEPROM #(.AddrBits(9), .isProgramMemory("true"), .Bits(8)) eeprom_3 (
    .A({in_1, _74377_1_pin19}), .CS(1'b1), .WE(1'b0), .OE(1'b1),
    .D({eeprom_3_d[7], H_sA, H_sB, H_sC, H_sD, H_sE, H_sF, H_sG}));
  _7486 _7486_2 (
    .pin1(SUB), .pin2(B1), .pin3(Y1), .pin4(SUB), .pin5(B2), .pin6(Y2), .pin7(1'b0), .pin8(Y3), .pin9(SUB),
    .pin10(B3), .pin11(Y4), .pin12(SUB), .pin13(B4), .pin14(1'b1));
  EEPROM #(.AddrBits(9), .isProgramMemory("true"), .Bits(8)) eeprom_4 (
    .A({in_1, _74377_1_pin19}), .CS(1'b1), .WE(1'b0), .OE(1'b1),
    .D({eeprom_4_d[7], T_sA, T_sB, T_sC, T_sD, T_sE, T_sF, T_sG}));
  EEPROM #(.AddrBits(9), .isProgramMemory("true"), .Bits(8)) eeprom_5 (
    .A({in_1, _74377_1_pin19}), .CS(1'b1), .WE(1'b0), .OE(1'b1),
    .D({eeprom_5_d[7], O_sA, O_sB, O_sC, O_sD, O_sE, O_sF, O_sG}));

  // Notes on the sheet:
  //   clk: Hz: 50
  //   Opcode Mnemonic | Operand | Description
  //   0x0 ····· LDA ······· | ······x······ | Load A from memory[x]
  //   0x1 ····· LDB ······· | ······x······ | Load B from memory[x]
  //   0x2 ····· LDAI ······ | ····imm··· | Load immediate value into A
  //   0x3 ····· LDBI ······ | ····imm··· | Load immediate value into B
  //   0x4 ····· STRA ····· | ······x······ | Store A into memory[x]
  //   0x5 ····· STRB ····· | ······x······ | Store B into memory[x]
  //   0x6 ····· STRI ······ | ····imm···· | Store A into address from immediate
  //   0x7 ····· ADD ······· | ······-······· | A = A + B; update ZF, CF
  //   0x8 ····· SUB ······· | ······-······· | A = A - B; update ZF, CF
  //   0x9 ····· ADDI ······ | ····imm··· | A = A + immediate; update ZF, CF
  //   0xA ····· SUBI ······ | ····imm··· | A = A - immediate; update ZF, CF
  //   0xB ····· JMP ······· | ······x······ | Jump unconditionally to x
  //   0xC ····· JZ ·········· | ······x······ | Jump to x if ZF is set
  //   0xD ····· JC ·········· | ······x······ | Jump to x if CF is set
  //   0xE ····· OUT ······· | ······-······ | Output A to display
  //   0xF ····· HLT ········ | ······-······ | Stop execution
  //   Microcode Counter
  //   Instruction Register
  //   Data Memory
  //   Instruction Memory
  //   Program Counter
  //   contents of eepromdualport_1 (hex, n*v repeats v):
  //   22,1,33,0,40,77,d0,ee,41,10,1,b4
  //   Instruction Decoder
  //   contents of eeprom_1 (hex, n*v repeats v):
  //   4002,1404,80800,20200,10000,11*0,4002,1404,80800,20010,10000,11*0
  //   ,4002,1404,4002,1204,10000,11*0,4002,1404,4002,1014,10000,11*0
  //   ,4002,1404,81000,40100,10000,11*0,4002,1404,81000,40020,10000
  //   ,11*0,4002,1404,81000,4002,41004,11*0,4002,1404,300280,10000,12*0
  //   ,4002,1404,3002c0,10000,12*0,4002,1404,4002,1010,300284,11*0,4002
  //   ,1404,4002,1010,3002c4,11*0,4002,1404,1001,10000,12*0,4002,1404
  //   ,10000,10000,12*0,4002,1404,10000,10000,12*0,4002,1404,108,10000
  //   ,12*0,4002,1404,8000,10000,12*0,4002,1404,80800,20200,10000,11*0
  //   ,4002,1404,80800,20010,10000,11*0,4002,1404,4002,1204,10000,11*0
  //   ,4002,1404,4002,1014,10000,11*0,4002,1404,81000,40100,10000,11*0
  //   ,4002,1404,81000,40020,10000,11*0,4002,1404,81000,4002,41004,11*0
  //   ,4002,1404,300280,10000,12*0,4002,1404,3002c0,10000,12*0,4002
  //   ,1404,4002,1010,300284,11*0,4002,1404,4002,1010,3002c4,11*0,4002
  //   ,1404,1001,10000,12*0,4002,1404,1001,10000,12*0,4002,1404,10000,10000
  //   ,12*0,4002,1404,108,10000,12*0,4002,1404,8000,10000,12*0,4002
  //   ,1404,80800,20200,10000,11*0,4002,1404,80800,20010,10000,11*0
  //   ,4002,1404,4002,1204,10000,11*0,4002,1404,4002,1014,10000,11*0
  //   ,4002,1404,81000,40100,10000,11*0,4002,1404,81000,40020,10000
  //   ,11*0,4002,1404,81000,4002,41004,11*0,4002,1404,300280,10000,12*0
  //   ,4002,1404,3002c0,10000,12*0,4002,1404,4002,1010,300284,11*0,4002
  //   ,1404,4002,1010,3002c4,11*0,4002,1404,1001,10000,12*0,4002,1404
  //   ,10000,10000,12*0,4002,1404,1001,10000,12*0,4002,1404,108,10000
  //   ,12*0,4002,1404,8000,10000,12*0,4002,1404,80800,20200,10000,11*0
  //   ,4002,1404,80800,20010,10000,11*0,4002,1404,4002,1204,10000,11*0
  //   ,4002,1404,4002,1014,10000,11*0,4002,1404,81000,40100,10000,11*0
  //   ,4002,1404,81000,40020,10000,11*0,4002,1404,81000,4002,41004,11*0
  //   ,4002,1404,300280,10000,12*0,4002,1404,3002c0,10000,12*0,4002
  //   ,1404,4002,1010,300284,11*0,4002,1404,4002,1010,3002c4,11*0,4002
  //   ,1404,1001,10000,12*0,4002,1404,1001,10000,12*0,4002,1404,1001
  //   ,10000,12*0,4002,1404,108,10000,12*0,4002,1404,8000,10000
  //   REGISTER A
  //   ALU
  //   REGISTER B
  //   OUTPUT
  //   UTILS
  //   FLAGS
  //   contents of eeprom_2 (hex, n*v repeats v):
  //   384*0,128*1
  //   contents of eeprom_3 (hex, n*v repeats v):
  //   100*7e,100*30,56*6d,100*7e,57*30,99*7e
  //   contents of eeprom_4 (hex, n*v repeats v):
  //   10*7e,10*30,10*6d,10*79,10*33,10*5b,10*5f,10*70,10*7f,10*7b,10*7e
  //   ,10*30,10*6d,10*79,10*33,10*5b,10*5f,10*70,10*7f,10*7b,10*7e,10*30
  //   ,10*6d,10*79,10*33,6*5b,10*7e,10*30,10*6d,10*79,10*33,10*5b,10*5f
  //   ,10*70,10*7f,10*7b,10*7e,10*30,17*6d,10*30,10*7e,10*7b,10*7f,10*70
  //   ,10*5f,10*5b,10*33,10*79,10*6d,10*30,9*7e
  //   contents of eeprom_5 (hex, n*v repeats v):
  //   7e,30,6d,79,33,5b,5f,70,7f,7b,7e,30,6d,79,33,5b,5f,70,7f,7b,7e
  //   ,30,6d,79,33,5b,5f,70,7f,7b,7e,30,6d,79,33,5b,5f,70,7f,7b,7e,30
  //   ,6d,79,33,5b,5f,70,7f,7b,7e,30,6d,79,33,5b,5f,70,7f,7b,7e,30,6d
  //   ,79,33,5b,5f,70,7f,7b,7e,30,6d,79,33,5b,5f,70,7f,7b,7e,30,6d,79
  //   ,33,5b,5f,70,7f,7b,7e,30,6d,79,33,5b,5f,70,7f,7b,7e,30,6d,79,33
  //   ,5b,5f,70,7f,7b,7e,30,6d,79,33,5b,5f,70,7f,7b,7e,30,6d,79,33,5b
  //   ,5f,70,7f,7b,7e,30,6d,79,33,5b,5f,70,7f,7b,7e,30,6d,79,33,5b,5f
  //   ,70,7f,7b,7e,30,6d,79,33,5b,5f,70,7f,7b,7e,30,6d,79,33,5b,5f,70
  //   ,7f,7b,7e,30,6d,79,33,5b,5f,70,7f,7b,7e,30,6d,79,33,5b,5f,70,7f
  //   ,7b,7e,30,6d,79,33,5b,5f,70,7f,7b,7e,30,6d,79,33,5b,5f,70,7f,7b
  //   ,7e,30,6d,79,33,5b,5f,70,7f,7b,7e,30,6d,79,33,5b,5f,70,7f,7b,7e
  //   ,30,6d,79,33,5b,5f,70,7f,7b,7e,30,6d,79,33,5b,5f,70,7f,7b,7e,30
  //   ,6d,79,33,5b,7e,30,6d,79,33,5b,5f,70,7f,7b,7e,30,6d,79,33,5b,5f
  //   ,70,7f,7b,7e,30,6d,79,33,5b,5f,70,7f,7b,7e,30,6d,79,33,5b,5f,70
  //   ,7f,7b,7e,30,6d,79,33,5b,5f,70,7f,7b,7e,30,6d,79,33,5b,5f,70,7f
  //   ,7b,7e,30,6d,79,33,5b,5f,70,7f,7b,7e,30,6d,79,33,5b,5f,70,7f,7b
  //   ,7e,30,6d,79,33,5b,5f,70,7f,7b,7e,30,6d,79,33,5b,5f,70,7f,7b,7e
  //   ,30,6d,79,33,5b,5f,70,7f,7b,7e,30,6d,79,33,5b,5f,70,7f,7b,7e,30
  //   ,6d,79,33,5b,5f,70,7f,70,5f,5b,33,79,6d,30,7e,7b,7f,70,5f,5b,33
  //   ,79,6d,30,7e,7b,7f,70,5f,5b,33,79,6d,30,7e,7b,7f,70,5f,5b,33,79
  //   ,6d,30,7e,7b,7f,70,5f,5b,33,79,6d,30,7e,7b,7f,70,5f,5b,33,79,6d
  //   ,30,7e,7b,7f,70,5f,5b,33,79,6d,30,7e,7b,7f,70,5f,5b,33,79,6d,30
  //   ,7e,7b,7f,70,5f,5b,33,79,6d,30,7e,7b,7f,70,5f,5b,33,79,6d,30,7e
  //   ,7b,7f,70,5f,5b,33,79,6d,30,7e,7b,7f,70,5f,5b,33,79,6d,30,7e,7b
  //   ,7f,70,5f,5b,33,79,6d,30
endmodule
